# Fritzing sketch BoardMarker (saved by Fritzing 0.9.3b)

parts:
  Part1 = Arduino Nano (Rev3.0) (ICSP)
  Part2 = NRF24L01+ Breakout Board
  Part3 = Arduino Nano (Rev3.0) (ICSP)
  Part4 = NRF24L01+ Breakout Board
  GY1 = MPU-6050 Board GY-521 [form="♀ (female)" package=THT]

nets:
  N1: Part1.D7, Part2.CE
  N2: Part1.D8, Part2.CS
  N3: Part1.D11/MOSI, Part2.MOSI
  N4: Part1.D12/MISO, Part2.MISO
  GND: Part1.GND, Part2.GND
  3V3: Part1.3V3, Part2.VCC
  N5: Part1.D13/SCK, Part2.SCK
  N6: Part3.D2, GY1.pin8
  N7: Part3.D7, Part3.D9, Part4.CE
  N8: Part3.D8, Part3.D10, Part4.CS
  N9: Part3.D11/MOSI, Part4.MOSI
  N10: Part3.D12/MISO, Part4.MISO
  GND_2: Part3.GND, Part4.GND, GY1.pin2
  N11: Part3.A5, GY1.pin3
  N12: Part3.A4, GY1.pin4
  3V3_2: Part3.3V3, Part4.VCC, GY1.pin1
  N13: Part3.D13/SCK, Part4.SCK

custom parts:
  MPU-6050 Board GY-521: Acelerometro y Giroscopio MPU-6050 Board GY-521
