# Fritzing sketch Audio Receiver (saved by Fritzing 0.9.3b)

parts:
  part = Arduino Nano (Rev3.0) (ICSP)
  part_2 = NRF24L01+ Breakout Board
  part_3 = Audio Jack (TRS) 3.5mm [package="4Ucon 08780 [THT]"]
  part_4 = Audio Jack (TRS) 3.5mm [package="4Ucon 08780 [THT]"]
  part_5 = Trimmer Potentiometer [maximum_resistance=100kΩ package=THT]
  part_6 = Ceramic Capacitor [capacitance="100 nF" package="0603 [SMD, multilayer]"]

nets:
  GND: part.GND, part_2.GND, part_3.Sleeve, part_4.Sleeve, part_5.leg2
  N1: part.D7, part_2.CE
  N2: part.D8, part_2.CS
  N3: part.D9, part_3.Tip
  N4: part.D10, part_3.Ring
  N5: part.D11/MOSI, part_2.MOSI
  N6: part.D12/MISO, part_2.MISO
  N7: part.5V, part_5.leg1
  N8: part.A0, part_5.wiper, part_6.0
  3V3: part.3V3, part_2.VCC
  N9: part.D13/SCK, part_2.SCK
  N10: part_4.Tip, part_6.1
