# Fritzing sketch Marker Receiver (saved by Fritzing 0.9.3b)

parts:
  Part1 = Arduino Nano (Rev3.0) (ICSP)
  Part2 = NRF24L01+ Breakout Board

nets:
  GND: Part1.GND, Part2.GND
  N1: Part1.D7, Part2.CE
  N2: Part1.D8, Part2.CS
  N3: Part1.D11/MOSI, Part2.MOSI
  N4: Part1.D12/MISO, Part2.MISO
  3V3: Part1.3V3, Part2.VCC
  N5: Part1.D13/SCK, Part2.SCK
