# Fritzing sketch Marker Transmitter (saved by Fritzing 0.9.3b)

parts:
  part = Arduino Nano (Rev3.0) (ICSP)
  part_2 = NRF24L01+ Breakout Board
  part_3 = RGB LED (com. cathode, rgb) [package="5 mm [THT]"]
  part_4 = LIPO-110mAh [package=lipo-110]
  GY1 = MPU-6050 Board GY-521 [form="♀ (female)" package=THT]

nets:
  GND: part.GND, part_2.GND, part_3.common_cathode, part_4.-, GY1.pin2
  N1: part.D3, part_3.blue_anode
  N2: part.D5, part_3.green_anode
  N3: part.D6, part_3.red_anode
  N4: part.D7, part_2.CE
  N5: part.D8, part_2.CS
  N6: part.D11/MOSI, part_2.MOSI
  N7: part.D12/MISO, part_2.MISO
  N8: part.VIN, part_4.+
  N9: part.5V, GY1.pin1
  N10: part.A5, GY1.pin3
  N11: part.A4, GY1.pin4
  3V3: part.3V3, part_2.VCC
  N12: part.D13/SCK, part_2.SCK

custom parts:
  MPU-6050 Board GY-521: Acelerometro y Giroscopio MPU-6050 Board GY-521
